# Fritzing sketch MCP4921 (saved by Fritzing 0.6.3b)
breadboards: 1

parts:
  MCP1 = MCP4801
  Arduino1 = Arduino

nets:
  N1: MCP1.connector0, Arduino1.+5V
  N2: MCP1.connector1, Arduino1.D9
  N3: MCP1.connector2, Arduino1.D13
  N4: MCP1.connector3, Arduino1.D11
  N5: MCP1.connector4, Arduino1.D8
  N6: MCP1.connector5, Arduino1.D10
  N7: MCP1.connector6, Arduino1.GND
